# Fritzing sketch 7-segment-wiring (saved by Fritzing 0.9.2b)
breadboards: 1

parts:
  Part1 = Arduino Uno (Rev3)
  R1 = Resistor [tolerance=±5% resistance=220 package=THT]
  7_Segment1 = 7-Segment LED Display [package=THT]

nets:
  N1: Part1.D8, 7_Segment1.cathodeG
  N2: Part1.D9_PWM, 7_Segment1.cathodeDP
  N3: Part1.D2, 7_Segment1.cathodeA
  N4: Part1.D3_PWM, 7_Segment1.cathodeB
  N5: Part1.D4, 7_Segment1.cathodeC
  N6: Part1.D5_PWM, 7_Segment1.cathodeD
  N7: Part1.D6_PWM, 7_Segment1.cathodeE
  N8: Part1.D7, 7_Segment1.cathodeF
  N9: Part1.5V, R1.Pin_1
  N10: R1.Pin_0, 7_Segment1.commAnode

notes:
  g | f | comm | a | b
  e | d | comm | c | h
  a | b | c | d | e | f | g | h
