# Fritzing sketch piezo-sensor-circuit (saved by Fritzing 0.9.2b)
breadboards: 1

parts:
  Part1 = Arduino Uno (Rev3)
  R1 = Resistor [tolerance=±5% resistance=1M package=THT]
  MIC1 = Microphone

nets:
  N1: Part1.A0, R1.Pin_1, MIC1.pin2
  N2: Part1.GND, R1.Pin_0, MIC1.pin1
